# Fritzing sketch led_connection (saved by Fritzing 0.9.6b)
breadboards: 1

parts:
  U1 = NodeMCU V1.0
  LED2 = smd LED [color="Red (633nm)" package="1206 [SMD]"]
  R1 = Resistor [tolerance=±5% resistance=220 package="1206 [SMD]"]
  R2 = Resistor [tolerance=±5% resistance=220 package="1206 [SMD]"]
  R3 = Resistor [tolerance=±5% resistance=220 package="1206 [SMD]"]
  LED1 = smd LED [color="Red (633nm)" package="1206 [SMD]"]
  LED3 = smd LED [color="Red (633nm)" package="1206 [SMD]"]

nets:
  N1: U1.D0, R1.Pin_1
  N2: U1.D1, R2.Pin_1
  N3: U1.D2, R3.Pin_1
  N4: U1.GND, LED2.cathode, LED1.cathode, LED3.cathode
  N5: LED2.anode, R1.Pin_0
  N6: R2.Pin_0, LED1.anode
  N7: R3.Pin_0, LED3.anode

custom parts:
  NodeMCU V1.0: ESP8266 based NodeMCU
